# Fritzing sketch Schaltplan (saved by Fritzing 1.0.6)
circuit board: 8.46667cm x 5.64444cm
breadboards: 1

parts:
  Power_plug1 = Power plug
  DotStar1 = DotStar LED Strip [mn=Adafruit mpn=2239 part_number=2239]
  Adafruit_Feather_ESP32-C1 = Adafruit Feather ESP32-C6 [mn=Adafruit mpn=#5933 part_number=#5933]
  Adafruit_Pixel_Shifter1 = Adafruit Pixel Shifter [mn=Adafruit mpn=#6066 part_number=#6066]

nets:
  GND: Power_plug1.GND, DotStar1.GND, Adafruit_Feather_ESP32-C1.GND, Adafruit_Pixel_Shifter1.GND
  VCC: Power_plug1.VCC, DotStar1.+5V
  N1: DotStar1.DI, Adafruit_Pixel_Shifter1.DAT_5V
  N2: Adafruit_Feather_ESP32-C1.IO15, Adafruit_Pixel_Shifter1.DAT_3V
